// Logisim project microprocessor1.circ as structural Verilog: 3 circuits, main circuit main
module main (
  input  in_1,
  output [7:0] out_2,
  output [7:0] out_3,
  output [7:0] out_4,
  output [2:0] out_5,
  output [7:0] out_6,
  output [7:0] out_7
);

  wire clk, Data, Load, LoadR, not_1_out, or_1_out, or_2_out, Store;
  wire [2:0] Rb;
  wire [7:0] PROGRAM_COUNTER_q;
  wire [9:0] Address;
  wire [15:0] ram_2_data;
  wire [15:13] INSTRUCTION_REGISTER_q;

  RAM #(.addrWidth(10)) ram_1 (.addr(Address), .data(out_2), .clk(clk), .ld(not_1_out));  // open: sel, clr
  not not_1 (not_1_out, Store);
  assign out_2 = Store ? out_6 : 8'bz;  // Controlled_Buffer controlled_buffer_1
  assign out_3 = Data ? out_4 : 8'bz;  // Controlled_Buffer controlled_buffer_2
  assign out_3 = Load ? out_2 : 8'bz;  // Controlled_Buffer controlled_buffer_3
  assign out_3 = LoadR ? Address[7:0] : 8'bz;  // Controlled_Buffer controlled_buffer_4
  assign out_5 = or_1_out ? Rb : 3'bz;  // Controlled_Buffer controlled_buffer_5
  or or_1 (or_1_out, LoadR, Load);
  assign out_5 = Data ? Address[5:3] : 3'bz;  // Controlled_Buffer controlled_buffer_6
  Counter PROGRAM_COUNTER (.count(1'b1), .Q(PROGRAM_COUNTER_q), .clk(clk), .clr(in_1));  // open: load, D, carry
  or or_2 (or_2_out, Data, Load, LoadR);
  Register_File REGISTER_BANK (
    .Clock(clk), .Input_value(out_3), .Write(or_2_out), .Destination_register__Rd(out_5), .Output_a(out_7),
    .Address_register_A__Ra(Address[2:0]), .Ouput_b(out_6), .Address_register_B__Rb(Rb));
  RAM #(.dataWidth(16)) ram_2 (.addr(PROGRAM_COUNTER_q), .data(ram_2_data), .clk(clk));  // open: sel, ld, clr
  _8bitALU ALU (.Input_A(out_7), .Input_B(out_6), .in_3(Address[9:6]), .RESULT(out_4));
  Register #(.width(16)) INSTRUCTION_REGISTER (
    .D(ram_2_data), .en(1'b1), .Q({INSTRUCTION_REGISTER_q, Address, Rb}), .clk(clk), .clr(1'b0));
  Clock clock_1 (.out(clk));
  and and_1 (Data, ~INSTRUCTION_REGISTER_q[15], ~INSTRUCTION_REGISTER_q[14], INSTRUCTION_REGISTER_q[13]);  // AND_Gate
  and and_2 (Load, ~INSTRUCTION_REGISTER_q[15], INSTRUCTION_REGISTER_q[14], ~INSTRUCTION_REGISTER_q[13]);  // AND_Gate
  and and_3 (Store, INSTRUCTION_REGISTER_q[15], ~INSTRUCTION_REGISTER_q[14], ~INSTRUCTION_REGISTER_q[13]);  // AND_Gate
  and and_4 (LoadR, ~INSTRUCTION_REGISTER_q[15], INSTRUCTION_REGISTER_q[14], INSTRUCTION_REGISTER_q[13]);  // AND_Gate

  // Other names for the same wires on the sheet: Ra[2:0] = Address[2:0]; Value[7:0] = Address[7:0];
  //   Rd[2:0] = Address[5:3]; Opcode[3:0] = Address[9:6]; Counter_reset = in_1

  // Notes on the sheet:
  //   DATA MEMORY
  //   INTERNAL BUS
  //   HARVARD ARCHITECTURE
  //   INSTRUCTION MEMORY
  //   INTERNAL BUS
  //   OPCODE
  //   0000 = Addition
  //   0001 = Subtraction
  //   0010 = Multiplication
  //   0011 = Division
  //   0100 = AND
  //   0101 = OR
  //   0110 = Negate(a)
  //   0111 = Negate(b)
  //   INSTRUCTION
  //   001 = Data
  //   010 = Load
  //   100 = Store
  //   011 = LoadR
  //   SYSTEM CLOCK
  //   HEXADECIMAL
  //   where X = Instruction
  //   XXXO  OOOA  AAQQ  QVVV 
  //   O = Opcode
  //   A = Destination register (Rd)
  //   Q = Address register A
  //   V = Address Register B
  //   Value = 10  9  8  7  6  5  4  3
  //   CONTROL UNIT
  //   Address = 12  11  10  9  8  7  6  5  4  3
  //   example: 6021  603a  20ca  803b
  //   4+7 = 11
endmodule

module Register_File (
  input  Clock,
  input  [7:0] Input_value,
  input  Write,
  input  [2:0] Address_register_A__Ra,
  input  [2:0] Address_register_B__Rb,
  input  [2:0] Destination_register__Rd,
  output [7:0] Output_a,
  output [7:0] Ouput_b
);

  wire and_1_out, and_2_out, and_3_out, and_4_out, and_5_out, and_6_out, and_7_out, and_8_out,
       decoder_1_out0, decoder_1_out1, decoder_1_out2, decoder_1_out3, decoder_1_out4, decoder_1_out5,
       decoder_1_out6, decoder_1_out7;
  wire [7:0] R0_q, R1_q, R2_q, R3_q, R4_q, R5_q, R6_q, R7_q;

  Decoder #(.select(3)) decoder_1 (
    .out0(decoder_1_out0), .out1(decoder_1_out1), .out2(decoder_1_out2), .out3(decoder_1_out3),
    .out4(decoder_1_out4), .out5(decoder_1_out5), .out6(decoder_1_out6), .out7(decoder_1_out7),
    .sel(Destination_register__Rd));  // open: en
  and and_1 (and_1_out, decoder_1_out0, Write);
  and and_2 (and_2_out, decoder_1_out1, Write);
  and and_3 (and_3_out, decoder_1_out2, Write);
  and and_4 (and_4_out, decoder_1_out3, Write);
  and and_5 (and_5_out, decoder_1_out4, Write);
  and and_6 (and_6_out, decoder_1_out5, Write);
  and and_7 (and_7_out, decoder_1_out6, Write);
  and and_8 (and_8_out, decoder_1_out7, Write);
  Register R0 (.D(Input_value), .en(and_1_out), .Q(R0_q), .clk(Clock), .clr(1'b0));
  Register R1 (.D(Input_value), .en(and_2_out), .Q(R1_q), .clk(Clock), .clr(1'b0));
  Register R2 (.D(Input_value), .en(and_3_out), .Q(R2_q), .clk(Clock), .clr(1'b0));
  Register R3 (.D(Input_value), .en(and_4_out), .Q(R3_q), .clk(Clock), .clr(1'b0));
  Register R4 (.D(Input_value), .en(and_5_out), .Q(R4_q), .clk(Clock), .clr(1'b0));
  Register R5 (.D(Input_value), .en(and_6_out), .Q(R5_q), .clk(Clock), .clr(1'b0));
  Register R6 (.D(Input_value), .en(and_7_out), .Q(R6_q), .clk(Clock), .clr(1'b0));
  Register R7 (.D(Input_value), .en(and_8_out), .Q(R7_q), .clk(Clock), .clr(1'b0));
  Multiplexer #(.select(3), .width(8)) multiplexer_1 (
    .in0(R0_q), .in1(R1_q), .in2(R2_q), .in3(R3_q), .in4(R4_q), .in5(R5_q), .in6(R6_q), .in7(R7_q),
    .out(Output_a), .sel(Address_register_A__Ra));  // open: en
  Multiplexer #(.select(3), .width(8)) multiplexer_2 (
    .in0(R0_q), .in1(R1_q), .in2(R2_q), .in3(R3_q), .in4(R4_q), .in5(R5_q), .in6(R6_q), .in7(R7_q),
    .out(Ouput_b), .sel(Address_register_B__Rb));  // open: en
endmodule

module _8bitALU (
  input  [7:0] Input_A,
  input  [7:0] Input_B,
  input  [3:0] in_3,
  output [7:0] RESULT
);

  wire [7:0] adder_1_out, and_1_out, divider_1_out, multiplier_1_out, negator_1_out, negator_2_out, or_1_out,
       subtractor_1_out;

  Adder adder_1 (.a(Input_A), .b(Input_B), .out(adder_1_out));  // open: cin, cout
  Subtractor subtractor_1 (.a(Input_A), .b(Input_B), .out(subtractor_1_out));  // open: bin, bout
  Multiplier multiplier_1 (.a(Input_A), .b(Input_B), .out(multiplier_1_out));  // open: cin, cout
  Divider divider_1 (.a(Input_A), .b(Input_B), .out(divider_1_out));  // open: upper, rem
  assign and_1_out = Input_A & Input_B;  // AND_Gate and_1, 8 bits wide
  assign or_1_out = Input_A | Input_B;  // OR_Gate or_1, 8 bits wide
  Negator negator_1 (.in(Input_A), .out(negator_1_out));
  Negator negator_2 (.in(Input_B), .out(negator_2_out));
  Multiplexer #(.select(4), .width(8)) multiplexer_1 (
    .in0(adder_1_out), .in1(subtractor_1_out), .in2(multiplier_1_out), .in3(divider_1_out), .in4(and_1_out),
    .in5(or_1_out), .in6(negator_1_out), .in7(negator_2_out), .out(RESULT), .sel(in_3));  // open: in8, in9, in10, in11, in12, in13, in14, in15, en
endmodule
